# Fritzing sketch uhppoted-wiegand-pico (saved by Fritzing 0.9.10b)
breadboards: 4

parts:
  M1 = RioRand LM2596
  Part1 = Adafruit 4-channel I2C-safe Bi-directional Logic Level Converter [part_number="Adafruit #757"]
  J2 = female pin header, 2 pins [form="♀ (female)"]
  LED3 = LED - 3mm [color="Orange (620nm)" current=0.030 package="3 mm [THT]"]
  LED4 = LED - 3mm [color="Red (633nm)" current=0.030 package="3 mm [THT]"]
  LED1 = LED - 3mm [color="Green (555nm)" current=0.030 package="3 mm [THT]"]
  R1 = Resistor [tolerance=±5% resistance=1k package="0402 [SMD]"]
  R3 = Resistor [tolerance=±5% resistance=1k package="0402 [SMD]"]
  R4 = Resistor [tolerance=±5% resistance=1k package="0402 [SMD]"]
  LED2 = LED - 3mm [color="Yellow (585nm)" current=0.030 package="3 mm [THT]"]
  BZR1 = Piezo Speaker
  J4 = female pin header, 2 pins [form="♀ (female)"]
  J5 = female pin header, 3 pins [form="♀ (female)"]
  Mod1 = Raspberry Pi Pico
  Part2 = Adafruit SDIO microSD Breakout
  R2 = Resistor [tolerance=±5% resistance=1k package="0402 [SMD]"]
  R5 = Resistor [tolerance=±5% resistance=1k package="0402 [SMD]"]
  J6 = Camdenboss CTB0158-2 [part_number=CTB0158-2 package=THT]
  J7 = Camdenboss CTB0158-5 [part_number=CTB0158-5 package=THT]

nets:
  N1: M1.Pin_1, J6.pin1, J7.pin1
  GND: M1.Pin_2, M1.Pin_4, Part1.GND, J2.pin2, J5.pin2, Mod1.pin_3, Mod1.pin_8, Mod1.pin_11, Mod1.pin_13, Mod1.pin_18, Mod1.pin_23, Mod1.pin_28, Mod1.pin_33, Mod1.pin_38, Mod1.pin_42, Part2.GND, J6.pin2, J7.pin2
  N2: M1.Pin_3, Part1.HV, J2.pin1, Mod1.pin_39
  N3: Part1.A3, Mod1.pin_26, Mod1.pin_27
  N4: Part1.A2, Mod1.pin_21, Mod1.pin_25
  N5: Part1.A1, Mod1.pin_22, Mod1.pin_24
  3.3V: Part1.LV, R1.Pin_0, R3.Pin_0, R4.Pin_0, BZR1.pin2, Mod1.pin_36, Part2.3.3V, R2.Pin_0
  N6: Part1.B3, J7.pin5
  N7: Part1.B2, J7.pin4
  N8: Part1.B1, J7.pin3
  N9: LED3.cathode, Mod1.pin_17
  N10: LED3.anode, R3.Pin_1
  N11: LED4.cathode, Mod1.pin_15
  N12: LED4.anode, R4.Pin_1
  N13: LED1.cathode, Mod1.pin_20
  N14: LED1.anode, R1.Pin_1
  N15: LED2.cathode, Mod1.pin_19
  N16: LED2.anode, R2.Pin_1
  N17: BZR1.pin1, R5.Pin_0
  N18: J4.pin1, Mod1.pin_2
  N19: J4.pin2, Mod1.pin_1
  N20: J5.pin1, Mod1.pin_43
  N21: J5.pin3, Mod1.pin_41
  N22: Mod1.pin_4, Part2.SCLK
  N23: Mod1.pin_5, Part2.DI
  N24: Mod1.pin_6, Part2.DO
  N25: Mod1.pin_7, Part2.CS
  N26: Mod1.pin_9, Part2.CARDDET
  N27: Mod1.pin_16, R5.Pin_1

custom parts:
  Adafruit 4-channel I2C-safe Bi-directional Logic Level Converter: Because the Arduino (and Basic Stamp) are 5V devices, and most modern sensors, displays, flash cards and modes are 3.3V-only, many makers find that they need to perform level shifting/conversion to protect the 3.3V device from 5V. We do have some other handy level shifters in the shop, from the DIP 74LVC245 to the fancy bi-directional TXB0108. However, neither of these are happy to work with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
  Raspberry Pi Pico: Raspberry Pi Pico. Based around the RP2040 microcontroller the Pico is a low cost microcontroller device bringing Raspberry Pi quality, cost, and easy of use to the microcontroller space. Jan 2021, Split part in to two versions: tht (this one) and SMD. This one will drill holes for a .1 in header in pcb to allow plugging in the module as well as providing pads to solder the module to the top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
